# Fritzing sketch shield IRled (saved by Fritzing 0.9.3b)
circuit board: 8.46667cm x 5.64444cm

parts:
  R1 = Resistor [tolerance=±5% resistance=1k package=THT]
  R2 = Resistor [tolerance=±5% resistance=100 package=THT]
  J1 = male pin header, 2 pins [form="♂ (male)"]
  WeMos_D1_Mini_Protoboard_Shield2 = WeMos D1 Mini Protoboard Shield
  Q1 = NPN-Transistor [package="TO92 [THT]"]

nets:
  N1: R1.Pin_0, WeMos_D1_Mini_Protoboard_Shield2.X5-Y10, WeMos_D1_Mini_Protoboard_Shield2.X5-Y11, Q1.B
  N2: R1.Pin_1, WeMos_D1_Mini_Protoboard_Shield2.D4, WeMos_D1_Mini_Protoboard_Shield2.X5-Y6, WeMos_D1_Mini_Protoboard_Shield2.X7-Y6
  5V: R2.Pin_0, WeMos_D1_Mini_Protoboard_Shield2.5V, WeMos_D1_Mini_Protoboard_Shield2.X4-Y8, WeMos_D1_Mini_Protoboard_Shield2.X7-Y8
  N3: R2.Pin_1, J1.pin1, WeMos_D1_Mini_Protoboard_Shield2.X4-Y2, WeMos_D1_Mini_Protoboard_Shield2.X4-Y4
  N4: J1.pin2, WeMos_D1_Mini_Protoboard_Shield2.X3-Y2, WeMos_D1_Mini_Protoboard_Shield2.X4-Y11, Q1.C
  GND: WeMos_D1_Mini_Protoboard_Shield2.G, WeMos_D1_Mini_Protoboard_Shield2.X6-Y11, WeMos_D1_Mini_Protoboard_Shield2.X7-Y7, Q1.E
