# Fritzing sketch shield conns (saved by Fritzing 0.9.3b)
circuit board: 10cm x 6cm

parts:
  WeMos_D1_Mini_Protoboard_Shield2 = WeMos D1 Mini Protoboard Shield
  J5 = male pin header, 2 pins [form="♂ (male)"]
  J6 = male pin header, 3 pins [form="♂ (male)"]
  J7 = male pin header, 3 pins [form="♂ (male)"]
  S1 = Pushbutton [package=THT]

nets:
  3.3V: WeMos_D1_Mini_Protoboard_Shield2.3V3, WeMos_D1_Mini_Protoboard_Shield2.X2-Y8, WeMos_D1_Mini_Protoboard_Shield2.X3-Y4, WeMos_D1_Mini_Protoboard_Shield2.X3-Y7, J5.pin1, J7.pin2
  N1: WeMos_D1_Mini_Protoboard_Shield2.D0, WeMos_D1_Mini_Protoboard_Shield2.X2-Y3, WeMos_D1_Mini_Protoboard_Shield2.X3-Y2, S1.leg1
  N2: WeMos_D1_Mini_Protoboard_Shield2.D5, WeMos_D1_Mini_Protoboard_Shield2.X2-Y4, J7.pin3
  N3: WeMos_D1_Mini_Protoboard_Shield2.D6, WeMos_D1_Mini_Protoboard_Shield2.X2-Y5, J6.pin1
  N4: WeMos_D1_Mini_Protoboard_Shield2.D7, WeMos_D1_Mini_Protoboard_Shield2.X2-Y6, J6.pin2
  N5: WeMos_D1_Mini_Protoboard_Shield2.D8, WeMos_D1_Mini_Protoboard_Shield2.X2-Y7, J6.pin3
  GND: WeMos_D1_Mini_Protoboard_Shield2.G, WeMos_D1_Mini_Protoboard_Shield2.X4-Y4, WeMos_D1_Mini_Protoboard_Shield2.X4-Y7, WeMos_D1_Mini_Protoboard_Shield2.X6-Y2, WeMos_D1_Mini_Protoboard_Shield2.X7-Y7, J5.pin2, J7.pin1, S1.leg0
